# Fritzing sketch Weather Radio (saved by Fritzing 0.9.1b)
breadboards: 3
stripboards: 1

parts:
  SPKR1 = Loudspeaker
  U1 = LM386 [package=dip08]
  Part1 = Arduino Mega 2560 (Rev3)
  C1 = Electrolytic Capacitor [capacitance=220µF voltage=50V package="300 mil [THT, electrolytic]"]
  C2 = Ceramic Capacitor [capacitance=47nF voltage=50V package="100 mil [THT, multilayer]"]
  R2 = Resistor [tolerance=±5% resistance=10 package=THT]
  R1 = Trimmer Potentiometer [maximum_resistance=10kΩ package=THT]
  Si1 = Si4707 Receiver
  BB2 = 4-Line Bi-Directional Level Shifter
  RTC1 = DS1307 RTC Breakout
  microSD1 = MicroSD Breakout
  LED1 = LED - 5mm [color="Red (633nm)" package="5 mm [THT]"]
  LED2 = LED - 5mm [color="Green (560nm)" package="5 mm [THT]"]
  R3 = Resistor [tolerance=±5% resistance=220 package=THT]
  R4 = Resistor [tolerance=±5% resistance=220 package=THT]
  Datalogging_Sheild_SPI_Pins = female pin header, 4 pins [form="♀ (female)"]

nets:
  GND: SPKR1.pin1, U1.-IN, U1.V-, Part1.GND, R2.Pin_0, R1.leg2, Si1.SEN, Si1.GND, BB2.GND, RTC1.GND, microSD1.GND, LED1.cathode, LED2.cathode
  N1: SPKR1.pin2, C1.-, C2.1
  N2: U1.+IN, R1.wiper
  N3: U1.OUT, C1.+
  5V: U1.V+, Part1.5V, BB2.HV, RTC1.5V, microSD1.5V
  N4: Part1.D21/SCL, BB2.B2, RTC1.SCL
  N5: Part1.D20/SDA, BB2.B3, RTC1.SDA
  3V3: Part1.3V3, Si1.v3.3, Si1.VCC, Si1.W1_VCC, Si1.W1_v3.3, BB2.LV
  N6: Part1.D2_PWM, Si1.INTn
  N7: Part1.D22, Si1.RSTn
  N8: Part1.D50, microSD1.DO, Datalogging_Sheild_SPI_Pins.pin3
  N9: Part1.D51, microSD1.DI, Datalogging_Sheild_SPI_Pins.pin2
  N10: Part1.D52, microSD1.CLK, Datalogging_Sheild_SPI_Pins.pin4
  N11: Part1.D53, microSD1.CS, Datalogging_Sheild_SPI_Pins.pin1
  N12: C2.0, R2.Pin_1
  N13: R1.leg1, Si1.ROUT
  N14: LED1.anode, R4.Pin_1
  N15: LED2.anode, R3.Pin_1

notes:
  Adafruit Data Logger Shield
  Pretend this is an Arduino Shield
  Red = 5 Volt Power
  Red Banded = 3.3 Volt Power
  Black = Ground
  Ochre = Audio Output Unamplified
  Ochre Banded = Audio Output Amplified
  Yellow = Digital Output
  Orange = I2C Data Bus
  Orange Banded = I2C Clock Bus
  Cyan = SPI MOSI
  Cyan Banded = SPI MISO
  Purple Banded = SPI Clock
  Yellow Banded = SPI Chip Select
  Blue = Plastic Jumper
  SPI Pin Mappings
  SPI Uno Mega
  SS 10 53
  MOSI 11 51
  MISO 12 50
  SCLK 13 52
  10 | 11 | 12 | 13

custom parts:
  Si4707 Receiver: This module is designed around the Silicon Labs Si4707 Weather Band Radio Receiver IC. It allows for reception of all NOAA Weather Radio transmitter frequencies and integrates its own S.A.M.E. (Specific Area Message Encoder) decoder. Module allows for reception of decoded alert messages and other receiver information via an I2C interface.
  4-Line Bi-Directional Level Shifter: 4-Channel Bi-Directional Level Shifter
  DS1307 RTC Breakout: DS1307 Real-time Clock Breakout Board with Battery
  MicroSD Breakout: 5V-ready microSD Breakout with Level Shifter
